// Logisim project s-mips.circ as structural Verilog: 19 circuits, main circuit S-MIPS Board
module S_MIPS_Board (
  input  DESHABILITAR_DISPATCHER,
  output halt
);

  wire button_1_out, CLK, CS, d_ff_1_q, LCLR, LoadRAM, LoadRAMOn, LW, R_R_W, R_W, ram_dispatcher_1_finished,
       RCS, Reset_out, RST, TTY_EN;
  wire [2:0] KDB;
  wire [3:0] LMask, Mask, ram_1_read_time, ram_1_write_time, RMask;
  wire [6:0] KDB_DATA, TTY_DATA;
  wire [15:0] Addr, LAddr, RAddr;
  wire [31:0] I0, I1, I2, I3, LData, ram_1_data_out_0, ram_1_data_out_1, ram_1_data_out_2, ram_1_data_out_3,
       RI0, RI1, RI2, RI3;

  TTY #(.rows(25), .cols(80)) tty_1 (.data(TTY_DATA), .clk(CLK), .we(TTY_EN), .clr(RST));
  not not_1 (LoadRAMOn, ram_dispatcher_1_finished);
  RAM_Dispatcher ram_dispatcher_1 (
    .WriteTime(ram_1_write_time), .Clock(CLK), .Data(LData), .Address(LAddr), .Mask(LMask),
    .Finished(ram_dispatcher_1_finished), .Write(LW), .CLR(LCLR));
  Keyboard #(.buflen(64)) keyboard_1 (.clk(CLK), .re(KDB[0]), .avail(KDB[2]), .data(KDB_DATA));  // open: clr
  RAM ram_1 (
    .Address(RAddr), .Data_Out_0(ram_1_data_out_0), .Data_Out_1(ram_1_data_out_1),
    .Data_Out_2(ram_1_data_out_2), .Data_Out_3(ram_1_data_out_3), .Data_In_0(RI0), .Data_In_1(RI1),
    .Data_In_2(RI2), .Data_In_3(RI3), .Mask(RMask), .nRead_Write(R_R_W), .Chip_Select(RCS),
    .Read_Time(ram_1_read_time), .Reset(button_1_out), .Write_Time(ram_1_write_time));
  Button button_1 (.out(button_1_out));
  D_Flip_Flop d_ff_1 (.clk(CLK), .D(1'b1), .Q(d_ff_1_q), .reset(Reset_out));  // open: Qn, preset, en
  Button Reset (.out(Reset_out));
  S_MIPS s_mips_1 (
    .Kbd_Enable(KDB[0]), .Address(Addr), .Kbd_Clear(KDB[1]), .Kbd_Available(KDB[2]), .RAM_In_0(I0),
    .Kbd_ASCII_Data(KDB_DATA), .RAM_In_1(I1), .TTY_Enable(TTY_EN), .RAM_In_2(I2), .RAM_In_3(I3),
    .TTY_ASCII_Data(TTY_DATA), .Reset(RST), .RAM_Out_0(ram_1_data_out_0), .Clock(CLK),
    .RAM_Out_1(ram_1_data_out_1), .Stop(halt), .RAM_Out_2(ram_1_data_out_2), .RAM_Out_3(ram_1_data_out_3),
    .Mask(Mask), .Read_Time(ram_1_read_time), .Write_Time(ram_1_write_time), .nRead_Write(R_W),
    .Chip_Select(CS));
  D_Flip_Flop d_ff_2 (.clk(CLK), .D(d_ff_1_q), .Qn(LCLR), .reset(Reset_out));  // open: Q, preset, en
  or or_1 (RST, LCLR, LoadRAM);
  Clock clock_1 (.out(CLK));
  Multiplexer #(.width(32), .enable("false")) multiplexer_1 (.in0(I0), .in1(LData), .out(RI0), .sel(LoadRAM));
  Multiplexer #(.width(32), .enable("false")) multiplexer_2 (.in0(I1), .in1(LData), .out(RI1), .sel(LoadRAM));
  Multiplexer #(.width(32), .enable("false")) multiplexer_3 (.in0(I2), .in1(LData), .out(RI2), .sel(LoadRAM));
  Multiplexer #(.width(32), .enable("false")) multiplexer_4 (.in0(I3), .in1(LData), .out(RI3), .sel(LoadRAM));
  and and_1 (LoadRAM, ~DESHABILITAR_DISPATCHER, LoadRAMOn);  // AND_Gate
  Multiplexer #(.width(16), .enable("false")) multiplexer_5 (.in0(Addr), .in1(LAddr), .out(RAddr), .sel(LoadRAM));
  Multiplexer #(.width(4), .enable("false")) multiplexer_6 (.in0(Mask), .in1(LMask), .out(RMask), .sel(LoadRAM));
  Multiplexer #(.enable("false")) multiplexer_7 (.in0(CS), .in1(LW), .out(RCS), .sel(LoadRAM));
  Multiplexer #(.enable("false")) multiplexer_8 (.in0(R_W), .in1(LW), .out(R_R_W), .sel(LoadRAM));

  // Notes on the sheet:
  //   NO MODIFICAR
  //   Keyboard
endmodule

module RAM (
  input  [15:0] Address,
  input  [31:0] Data_In_0,
  input  [31:0] Data_In_1,
  input  [31:0] Data_In_2,
  input  [31:0] Data_In_3,
  input  [3:0] Mask,
  input  nRead_Write,
  input  Chip_Select,
  input  Reset,
  output [31:0] Data_Out_0,
  output [31:0] Data_Out_1,
  output [31:0] Data_Out_2,
  output [31:0] Data_Out_3,
  output [3:0] Read_Time,
  output [3:0] Write_Time
);

  wire and_2_out, and_3_out, and_4_out, and_5_out, and_6_out, and_7_out, and_8_out, and_9_out, Changed, CLK,
       comparator_2_eq, comparator_3_eq, comparator_4_eq, comparator_5_eq, comparator_6_eq, Count,
       demultiplexer_3_out0, Idle, Idle_q, Load, Load0, Load1, nand_1_out, or_1_out, or_2_out, or_3_out,
       or_4_out, or_5_out, or_6_out, or_7_out, or_8_out, or_9_out, or_10_out, Proc_q, Update_Mem, Zero_Time;
  wire [3:0] counter_1_q, multiplexer_1_out, subtractor_1_out;
  wire [31:0] register_1_q, register_2_q, register_3_q, register_4_q, register_5_q;

  // Probe on 4'b0011
  // Probe on 4'b0010
  Multiplexer #(.width(4), .enable("false")) multiplexer_1 (
    .in0(4'b0011), .in1(4'b0010), .out(multiplexer_1_out), .sel(nRead_Write));
  or or_1 (or_1_out, Idle, Update_Mem);
  or or_2 (or_2_out, ~Chip_Select, Reset);  // OR_Gate
  Subtractor #(.width(4)) subtractor_1 (.a(multiplexer_1_out), .b(4'b0010), .out(subtractor_1_out));  // open: bin, bout
  Demultiplexer #(.enable("false")) demultiplexer_1 (.out0(Idle), .out1(Load0), .in(Idle_q), .sel(Changed));
  D_Flip_Flop u_Idle (.clk(CLK), .D(or_1_out), .Q(Idle_q), .preset(or_2_out));  // open: Qn, en, reset
  // Probe on counter_1_q
  Counter #(.width(4), .max('hf)) counter_1 (
    .load(Load), .D(subtractor_1_out), .count(Count), .Q(counter_1_q), .clk(CLK), .clr(or_3_out));  // open: carry
  or or_3 (or_3_out, ~Chip_Select, Reset);  // OR_Gate
  Comparator #(.width(4), .mode("unsigned")) comparator_1 (
    .a(4'b0000), .b(counter_1_q), .eq(Zero_Time));  // open: gt, lt
  or or_4 (or_4_out, Count, Load0, Load1);
  Register #(.width(32)) register_1 (.D(Data_In_0), .en(Chip_Select), .Q(register_1_q), .clk(CLK), .clr(or_5_out));
  or or_5 (or_5_out, ~Chip_Select, Reset);  // OR_Gate
  Register #(.width(32)) register_2 (.D(Data_In_1), .en(Chip_Select), .Q(register_2_q), .clk(CLK), .clr(or_6_out));
  or or_6 (or_6_out, ~Chip_Select, Reset);  // OR_Gate
  Register #(.width(32)) register_3 (.D(Data_In_2), .en(Chip_Select), .Q(register_3_q), .clk(CLK), .clr(or_7_out));
  or or_7 (or_7_out, ~Chip_Select, Reset);  // OR_Gate
  Register #(.width(32)) register_4 (.D(Data_In_3), .en(Chip_Select), .Q(register_4_q), .clk(CLK), .clr(or_8_out));
  or or_8 (or_8_out, ~Chip_Select, Reset);  // OR_Gate
  Register #(.width(32)) register_5 (
    .D({{11{1'b1}}, nRead_Write, Mask, Address}), .en(Chip_Select), .Q(register_5_q), .clk(CLK),
    .clr(or_9_out));
  or or_9 (or_9_out, ~Chip_Select, Reset);  // OR_Gate
  D_Flip_Flop Proc (.clk(CLK), .D(or_4_out), .Q(Proc_q), .reset(or_10_out));  // open: Qn, preset, en
  or or_10 (or_10_out, ~Chip_Select, Reset);  // OR_Gate
  Demultiplexer #(.enable("false")) demultiplexer_2 (
    .out0(Count), .out1(Update_Mem), .in(demultiplexer_3_out0), .sel(Zero_Time));
  Demultiplexer #(.enable("false")) demultiplexer_3 (
    .out0(demultiplexer_3_out0), .out1(Load1), .in(Proc_q), .sel(Changed));
  Clock clock_1 (.out(CLK));
  Comparator #(.width(32)) comparator_2 (.a(register_1_q), .b(Data_In_0), .eq(comparator_2_eq));  // open: gt, lt
  Comparator #(.width(32)) comparator_3 (.a(register_2_q), .b(Data_In_1), .eq(comparator_3_eq));  // open: gt, lt
  Comparator #(.width(32)) comparator_4 (.a(register_3_q), .b(Data_In_2), .eq(comparator_4_eq));  // open: gt, lt
  Comparator #(.width(32)) comparator_5 (.a(register_4_q), .b(Data_In_3), .eq(comparator_5_eq));  // open: gt, lt
  Comparator #(.width(32)) comparator_6 (
    .a(register_5_q), .b({{11{1'b1}}, nRead_Write, Mask, Address}), .eq(comparator_6_eq));  // open: gt, lt
  nand nand_1 (nand_1_out, comparator_6_eq, comparator_2_eq, comparator_3_eq, comparator_4_eq, comparator_5_eq);
  and and_1 (Changed, nand_1_out, Chip_Select);
  or or_11 (Load, Count, Load1, Load0);
  and and_2 (and_2_out, Mask[0], Update_Mem, nRead_Write);
  and and_3 (and_3_out, Mask[1], Update_Mem, nRead_Write);
  and and_4 (and_4_out, Mask[2], Update_Mem, nRead_Write);
  and and_5 (and_5_out, Mask[3], Update_Mem, nRead_Write);
  RAM_part #(.addrWidth(16), .dataWidth(32), .bus("separate")) ram_1 (
    .addr(Address), .din(Data_In_0), .data(Data_Out_0), .str(and_2_out), .sel(Chip_Select), .clk(CLK),
    .ld(and_6_out), .clr(Reset));
  and and_6 (and_6_out, ~nRead_Write, Idle);  // AND_Gate
  RAM_part #(.addrWidth(16), .dataWidth(32), .bus("separate")) ram_2 (
    .addr(Address), .din(Data_In_1), .data(Data_Out_1), .str(and_3_out), .sel(Chip_Select), .clk(CLK),
    .ld(and_7_out), .clr(Reset));
  and and_7 (and_7_out, ~nRead_Write, Idle);  // AND_Gate
  RAM_part #(.addrWidth(16), .dataWidth(32), .bus("separate")) ram_3 (
    .addr(Address), .din(Data_In_2), .data(Data_Out_2), .str(and_4_out), .sel(Chip_Select), .clk(CLK),
    .ld(and_8_out), .clr(Reset));
  and and_8 (and_8_out, ~nRead_Write, Idle);  // AND_Gate
  RAM_part #(.addrWidth(16), .dataWidth(32), .bus("separate")) ram_4 (
    .addr(Address), .din(Data_In_3), .data(Data_Out_3), .str(and_5_out), .sel(Chip_Select), .clk(CLK),
    .ld(and_9_out), .clr(Reset));
  and and_9 (and_9_out, ~nRead_Write, Idle);  // AND_Gate

  assign Read_Time = 4'b0011;
  assign Write_Time = 4'b0010;

  // Other names for the same wires on the sheet: M0 = Mask[0]; M1 = Mask[1]; M2 = Mask[2]; M3 = Mask[3];
  //   RW = nRead_Write; CLR = Reset; CS = Chip_Select; Load2 = Count

  // Notes on the sheet:
  //   NO MODIFICAR
  //   excepto quizás los valores RT y WT
  //   BANK0
  //   BANK1
  //   BANK2
  //   BANK3
endmodule

module S_MIPS (
  input  Kbd_Available,
  input  [6:0] Kbd_ASCII_Data,
  input  [31:0] RAM_Out_0,
  input  [31:0] RAM_Out_1,
  input  Reset,
  input  [31:0] RAM_Out_2,
  input  Clock,
  input  [31:0] RAM_Out_3,
  input  [3:0] Read_Time,
  input  [3:0] Write_Time,
  output Kbd_Enable,
  output [15:0] Address,
  output Kbd_Clear,
  output TTY_Enable,
  output [6:0] TTY_ASCII_Data,
  output Stop,
  output [31:0] RAM_In_0,
  output [31:0] RAM_In_1,
  output [31:0] RAM_In_2,
  output [31:0] RAM_In_3,
  output [3:0] Mask,
  output nRead_Write,
  output Chip_Select
);

  wire ALU_inst, get_data, get_inst, halt, jmp_inst, mem_inst, or_1_out, PC_en, R_inst, ready_data,
       ready_inst, ready_write, RF_en, stack_inst, start, tty, write, write_inst;
  wire [31:0] address_t, instruction;

  Data_Path data_path_1 (
    .in_3(Clock), .in_4(RF_en), .in_5(Reset), .in_6(Kbd_Available), .in_7(ready_inst), .in_8(PC_en),
    .in_2(Kbd_ASCII_Data), .Output_9(TTY_ASCII_Data), .in_9(get_inst), .Output(halt), .Output_2(ALU_inst),
    .Output_5(R_inst), .Output_6(jmp_inst), .Output_10(address_t), .Output_3(tty), .Output_4(mem_inst),
    .Output_7(stack_inst), .Output_8(write_inst), .R_out(RAM_In_0), .in_1(instruction));
  D_Flip_Flop #(.trigger("falling")) d_ff_1 (.clk(Clock), .D(Reset), .Q(start));  // open: Qn, preset, en, reset
  or or_1 (or_1_out, stack_inst, mem_inst);
  Control_Unit control_unit_1 (
    .in_2(start), .in_5(ready_inst), .in_6(ALU_inst), .in_9(R_inst), .in_10(Reset), .in_3(tty),
    .in_4(ready_data), .in_7(jmp_inst), .in_8(or_1_out), .in_11(write_inst), .in_12(ready_write),
    .Output(RF_en), .Output_2(PC_en), .Output_4(Stop), .Output_5(get_data), .Output_3(get_inst),
    .Output_6(TTY_Enable), .Output_7(Kbd_Enable), .Output_8(write), .in_1(Clock));
  \Caché_INTERACTION  \caché_interaction_1  (
    .bank0(RAM_Out_0), .bank1(RAM_Out_1), .bank2(RAM_Out_2), .bank3(RAM_Out_3), .dp_address(address_t),
    .read_time(Read_Time), .write_time(Write_Time), .address(Address), .mask(Mask), .get_data(get_data),
    .cs(Chip_Select), .rw(nRead_Write), .ready_inst(ready_inst), .write(write), .get_inst(get_inst),
    .clock(Clock), .reset(Reset), .ready_data(ready_data), .ready_write(ready_write),
    .Instruction(instruction), .in_6(RAM_In_0));

  assign Kbd_Clear = Reset;
  assign RAM_In_1 = RAM_In_0;
  assign RAM_In_2 = RAM_In_0;
  assign RAM_In_3 = RAM_In_0;

  // Other names for the same wires on the sheet: CLK = Clock; CS = Chip_Select; KBD_AVAIL = Kbd_Available;
  //   CLR = Reset; KBD_CLR = Reset; KBD_DATA[6:0] = Kbd_ASCII_Data; R_out[31:0] = RAM_In_0;
  //   RAM_INPUT_0[31:0] = RAM_In_0; RAM_INPUT_1[31:0] = RAM_In_0; RAM_INPUT_2[31:0] = RAM_In_0;
  //   RAM_INPUT_3[31:0] = RAM_In_0; RAM_A[15:0] = Address; RAM_MASK[3:0] = Mask; RAM_OUTPUT_0[31:0] = RAM_Out_0;
  //   RAM_OUTPUT_1[31:0] = RAM_Out_1; RAM_OUTPUT_2[31:0] = RAM_Out_2; RAM_OUTPUT_3[31:0] = RAM_Out_3;
  //   RW = nRead_Write; TTY_DATA[6:0] = TTY_ASCII_Data

  // Notes on the sheet:
  //   RAM ADDRESS
  //   DATA FROM RAM
  //   DATA TO RAM
  //   DATA WRITE MASK
  //   RAM TIMING
  //   RAM CONTROL
  //   KEYBOARD
  //   TTY
  //   SEQUENCING
  //   S-MIPS
  //   RAM INTERACTION
endmodule

module RAM_Dispatcher (
  input  [3:0] WriteTime,
  input  Clock,
  input  CLR,
  output [31:0] Data,
  output [15:0] Address,
  output [3:0] Mask,
  output Finished,
  output Write
);

  wire demultiplexer_2_out1, demultiplexer_3_out1, End, IDLE_q, IncAddr, Load, or_1_out, or_2_out, While_q,
       WriteEnd;
  wire [3:0] counter_1_q;
  wire [31:0] CurrentAddress_q;

  Counter #(.width(32), .max('hffffffff)) CurrentAddress (
    .count(IncAddr), .Q({CurrentAddress_q[31:18], Address, CurrentAddress_q[1:0]}), .clk(Clock), .clr(CLR));  // open: load, D, carry
  or or_1 (or_1_out, IncAddr, demultiplexer_3_out1, Finished);
  D_Flip_Flop IDLE (.clk(Clock), .D(or_1_out), .Q(IDLE_q), .preset(CLR));  // open: Qn, en, reset
  Demultiplexer #(.enable("false")) demultiplexer_1 (.out0(Load), .out1(Finished), .in(IDLE_q), .sel(End));
  D_Flip_Flop While (.clk(Clock), .D(or_2_out), .Q(While_q), .reset(CLR));  // open: Qn, preset, en
  or or_2 (or_2_out, Write, Load);
  RAM_part #(.addrWidth(18), .dataWidth(32)) ram_1 (
    .addr({Address, CurrentAddress_q[1:0]}), .data(Data), .clk(Clock));  // open: sel, ld, clr
  Demultiplexer #(.enable("false")) demultiplexer_2 (
    .out0(Write), .out1(demultiplexer_2_out1), .in(While_q), .sel(WriteEnd));
  Decoder #(.select(2)) decoder_1 (
    .out0(Mask[0]), .out1(Mask[1]), .out2(Mask[2]), .out3(Mask[3]), .sel(CurrentAddress_q[1:0]));  // open: en
  Demultiplexer #(.enable("false")) demultiplexer_3 (
    .out0(IncAddr), .out1(demultiplexer_3_out1), .in(demultiplexer_2_out1), .sel(End));
  Counter #(.width(4), .max('hf)) counter_1 (
    .load(Load), .D(WriteTime), .count(Write), .Q(counter_1_q), .clk(Clock));  // open: carry, clr
  Comparator #(.width(32)) comparator_1 (.a(Data), .b({32{1'b1}}), .eq(End));  // open: gt, lt
  Comparator #(.width(4)) comparator_2 (.a(4'b0000), .b(counter_1_q), .eq(WriteEnd));  // open: gt, lt

  // Other names for the same wires on the sheet: CLK = Clock; Count = Write; WT[3:0] = WriteTime
endmodule

module Multiplicador (
  input  [31:0] in_1,
  input  [31:0] in_2,
  input  in_3,
  output [31:0] HI,
  output [31:0] LO
);

  wire [31:0] adder_1_out, HI_t, HIU, multiplexer_1_out, multiplexer_2_out;

  Multiplexer #(.width(32), .enable("false")) multiplexer_1 (
    .in0({32{1'b0}}), .in1(in_1), .out(multiplexer_1_out), .sel(in_2[31]));
  Multiplexer #(.width(32), .enable("false")) multiplexer_2 (
    .in0({32{1'b0}}), .in1(in_1), .out(multiplexer_2_out), .sel(in_2[31]));
  Adder #(.width(32)) adder_1 (.a(multiplexer_1_out), .b(multiplexer_2_out), .out(adder_1_out));  // open: cin, cout
  Multiplier #(.width(32)) multiplier_1 (.a(in_1), .b(in_2), .out(LO), .cout(HI_t));  // open: cin
  Adder #(.width(32)) adder_2 (.a(HI_t), .b(adder_1_out), .out(HIU));  // open: cin, cout
  Multiplexer #(.width(32), .enable("false")) multiplexer_3 (.in0(HIU), .in1(HI_t), .out(HI), .sel(in_3));

  // Other names for the same wires on the sheet: a[31:0] = in_1; b[31:0] = in_2; sign = in_3

  // Notes on the sheet:
  //   Multiplicador
endmodule

module Divisor (
  input  [31:0] in_1,
  input  [31:0] in_2,
  input  in_3,
  output [31:0] out_4,
  output [31:0] out_5
);

  wire neg_a, neg_b, neg_div, xor_2_out;
  wire [31:0] abs_a, abs_b, abs_div, adder_1_out, divider_1_out, multiplexer_2_out, negator_1_out,
       negator_2_out, negator_3_out, negator_4_out, R, subtractor_1_out;

  Negator #(.width(32)) negator_1 (.in(in_1), .out(negator_1_out));
  xor xor_1 (neg_div, neg_a, neg_b);
  Divider #(.width(32)) divider_1 (.a(abs_a), .b(abs_b), .out(divider_1_out), .rem(R));  // open: upper
  and and_1 (neg_a, in_1[31], in_3);
  and and_2 (neg_b, in_3, in_2[31]);
  Multiplexer #(.width(32), .enable("false")) multiplexer_1 (.in0(in_1), .in1(negator_1_out), .out(abs_a), .sel(neg_a));
  Adder #(.width(32)) adder_1 (.a(divider_1_out), .out(adder_1_out), .cin(1'b1));  // open: b, cout
  Negator #(.width(32)) negator_2 (.in(abs_div), .out(negator_2_out));
  Multiplexer #(.width(32), .enable("false")) multiplexer_2 (
    .in0(divider_1_out), .in1(adder_1_out), .out(multiplexer_2_out), .sel(neg_a));
  Subtractor #(.width(32)) subtractor_1 (.a(abs_b), .b(R), .out(subtractor_1_out));  // open: bin, bout
  Negator #(.width(32)) negator_3 (.in(in_2), .out(negator_3_out));
  Multiplexer #(.width(32), .enable("false")) multiplexer_3 (
    .in0(abs_div), .in1(negator_2_out), .out(out_4), .sel(neg_div));
  Negator #(.width(32)) negator_4 (.in(multiplexer_2_out), .out(negator_4_out));
  xor xor_2 (xor_2_out, neg_a, neg_b);
  Multiplexer #(.width(32), .enable("false")) multiplexer_4 (.in0(in_2), .in1(negator_3_out), .out(abs_b), .sel(neg_b));
  Multiplexer #(.width(32), .enable("false")) multiplexer_5 (
    .in0(multiplexer_2_out), .in1(negator_4_out), .out(out_4), .sel(xor_2_out));
  Multiplexer #(.width(32), .enable("false")) multiplexer_6 (.in0(R), .in1(subtractor_1_out), .out(out_5), .sel(neg_a));

  // Other names for the same wires on the sheet: a[31:0] = in_1; b[31:0] = in_2; div[31:0] = out_4;
  //   remainder[31:0] = out_5; sign = in_3

  // Notes on the sheet:
  //   Divisor
endmodule

module ALU (
  input  in_1,
  input  in_2,
  input  [31:0] Input,
  input  [31:0] Input_2,
  input  [3:0] in_5,
  output [31:0] Output,
  output [31:0] Output_2,
  output [31:0] Output_3
);

  wire div, enable, mult;
  wire [31:0] add, \and , div_rem, div_res, mult_high, mult_low, multiplexer_2_out, multiplexer_3_out,
       \nand , \nor , \or , slt, sub, \xor ;

  assign \and  = Input & Input_2;  // AND_Gate and_1, 32 bits wide
  assign \or  = Input | Input_2;  // OR_Gate or_1, 32 bits wide
  assign \nand  = ~(Input & Input_2);  // NAND_Gate nand_1, 32 bits wide
  assign \nor  = ~(Input | Input_2);  // NOR_Gate nor_1, 32 bits wide
  assign \xor  = Input ^ Input_2;  // XOR_Gate xor_1, 32 bits wide
  Adder #(.width(32)) adder_1 (.a(Input), .b(Input_2), .out(add));  // open: cin, cout
  Subtractor #(.width(32)) subtractor_1 (.a(Input), .b(Input_2), .out(sub));  // open: bin, bout
  Comparador__SLT comparador_slt_1 (.in_1(Input), .in_3(in_2), .in_2(Input_2), .Output(slt));
  and and_2 (mult, ~in_5[0], in_5[1], ~in_5[2], ~in_5[3]);  // AND_Gate
  and and_3 (div, in_5[0], in_5[1], ~in_5[2], ~in_5[3]);  // AND_Gate
  Divisor divisor_1 (.in_1(Input), .in_3(in_2), .in_2(Input_2), .out_4(div_res), .out_5(div_rem));
  Multiplicador multiplicador_1 (.in_1(Input), .in_3(in_2), .in_2(Input_2), .HI(mult_high), .LO(mult_low));
  or or_2 (enable, mult, div);
  Multiplexer #(.select(4), .width(32), .enable("false")) multiplexer_1 (
    .in0(add), .in1(sub), .in4(slt), .in5(\and ), .in6(\or ), .in7(\nor ), .in8(\xor ), .out(Output),
    .sel(in_5));  // open: in2, in3, in9, in10, in11, in12, in13, in14, in15
  Multiplexer #(.width(32), .enable("false")) multiplexer_2 (
    .in0(mult_low), .in1(div_res), .out(multiplexer_2_out), .sel(div));
  Multiplexer #(.width(32), .enable("false")) multiplexer_3 (
    .in0(mult_high), .in1(div_rem), .out(multiplexer_3_out), .sel(div));
  Register #(.width(32)) register_1 (.D(multiplexer_2_out), .en(enable), .Q(Output_2), .clk(in_1));  // open: clr
  Register #(.width(32)) register_2 (.D(multiplexer_3_out), .en(enable), .Q(Output_3), .clk(in_1));  // open: clr

  // Other names for the same wires on the sheet: a[31:0] = Input; b[31:0] = Input_2; clock = in_1;
  //   HI[31:0] = Output_3; LO[31:0] = Output_2; _0 = in_5[0]; selector[3:0] = in_5; _1 = in_5[1]; _2 = in_5[2];
  //   _3 = in_5[3]; sign = in_2

  // Notes on the sheet:
  //   ALU
endmodule

module Comparador__SLT (
  input  [31:0] in_1,
  input  [31:0] in_2,
  input  in_3,
  output [31:0] Output
);

  wire multiplexer_1_out, slt, sltu;

  Comparator #(.width(32)) comparator_1 (.a(in_1), .b(in_2), .lt(slt));  // open: gt, eq
  Comparator #(.width(32), .mode("unsigned")) comparator_2 (.a(in_1), .b(in_2), .lt(sltu));  // open: gt, eq
  Multiplexer #(.enable("false")) multiplexer_1 (.in0(sltu), .in1(slt), .out(multiplexer_1_out), .sel(in_3));
  assign Output = {{31{1'b0}}, multiplexer_1_out};  // Bit_Extender bit_extender_1

  // Other names for the same wires on the sheet: a[31:0] = in_1; b[31:0] = in_2; sign = in_3

  // Notes on the sheet:
  //   SLT
endmodule

module Register_File (
  input  [4:0] in_1,
  input  [4:0] in_2,
  input  [4:0] in_3,
  input  in_4,
  input  in_5,
  input  in_6,
  input  in_7,
  input  in_8,
  input  in_9,
  input  [31:0] in_10,
  output [31:0] Output,
  output [31:0] Output_2,
  output [31:0] Output_3
);

  wire input31, L0, L1, L2, L3, L4, L5, L6, L7, L8, L9, L10, L11, L12, L13, L14, L15, L16, L17, L18, L19,
       L20, L21, L22, L23, L24, L25, L26, L27, L28, L29, L30, L31, or_1_out, or_2_out;
  wire [31:0] adder_1_out, multiplexer_2_out, out0, out1, out2, out3, out4, out5, out6, out7, out8, out9,
       out10, out11, out12, out13, out14, out15, out16, out17, out18, out19, out20, out21, out22, out23,
       out24, out25, out26, out27, out28, out29, out30, SP, subtractor_1_out;

  Demultiplexer #(.select(5), .enable("false")) demultiplexer_1 (
    .out0(L0), .out1(L1), .out2(L2), .out3(L3), .out4(L4), .out5(L5), .out6(L6), .out7(L7), .out8(L8),
    .out9(L9), .out10(L10), .out11(L11), .out12(L12), .out13(L13), .out14(L14), .out15(L15), .out16(L16),
    .out17(L17), .out18(L18), .out19(L19), .out20(L20), .out21(L21), .out22(L22), .out23(L23), .out24(L24),
    .out25(L25), .out26(L26), .out27(L27), .out28(L28), .out29(L29), .out30(L30), .out31(input31), .in(in_5),
    .sel(in_3));
  Register #(.width(32)) register_1 (.D({32{1'b0}}), .en(L0), .Q(out0), .clk(in_6), .clr(in_4));
  // Probe on out8
  Register #(.width(32)) register_2 (.D(in_10), .en(L8), .Q(out8), .clk(in_6), .clr(in_4));
  Register #(.width(32)) register_3 (.D(in_10), .en(L16), .Q(out16), .clk(in_6), .clr(in_4));
  Register #(.width(32)) register_4 (.D(in_10), .en(L24), .Q(out24), .clk(in_6), .clr(in_4));
  Register #(.width(32)) register_5 (.D(in_10), .en(L1), .Q(out1), .clk(in_6), .clr(in_4));
  Register #(.width(32)) register_6 (.D(in_10), .en(L9), .Q(out9), .clk(in_6), .clr(in_4));
  Register #(.width(32)) register_7 (.D(in_10), .en(L17), .Q(out17), .clk(in_6), .clr(in_4));
  Register #(.width(32)) register_8 (.D(in_10), .en(L25), .Q(out25), .clk(in_6), .clr(in_4));
  or or_1 (or_1_out, in_8, in_9);
  and and_1 (L31, in_7, or_1_out);
  Register #(.width(32)) register_9 (.D(in_10), .en(L2), .Q(out2), .clk(in_6), .clr(in_4));
  Register #(.width(32)) register_10 (.D(in_10), .en(L10), .Q(out10), .clk(in_6), .clr(in_4));
  Register #(.width(32)) register_11 (.D(in_10), .en(L18), .Q(out18), .clk(in_6), .clr(in_4));
  Register #(.width(32)) register_12 (.D(in_10), .en(L26), .Q(out26), .clk(in_6), .clr(in_4));
  Register #(.width(32)) register_13 (.D(in_10), .en(L3), .Q(out3), .clk(in_6), .clr(in_4));
  Register #(.width(32)) register_14 (.D(in_10), .en(L11), .Q(out11), .clk(in_6), .clr(in_4));
  Register #(.width(32)) register_15 (.D(in_10), .en(L19), .Q(out19), .clk(in_6), .clr(in_4));
  Register #(.width(32)) register_16 (.D(in_10), .en(L27), .Q(out27), .clk(in_6), .clr(in_4));
  Register #(.width(32)) register_17 (.D(in_10), .en(L4), .Q(out4), .clk(in_6), .clr(in_4));
  Register #(.width(32)) register_18 (.D(in_10), .en(L12), .Q(out12), .clk(in_6), .clr(in_4));
  Register #(.width(32)) register_19 (.D(in_10), .en(L20), .Q(out20), .clk(in_6), .clr(in_4));
  Register #(.width(32)) register_20 (.D(in_10), .en(L28), .Q(out28), .clk(in_6), .clr(in_4));
  Subtractor #(.width(32)) subtractor_1 (.a(Output_2), .b(32'h4), .out(subtractor_1_out));  // open: bin, bout
  Adder #(.width(32)) adder_1 (.a(32'h4), .b(Output_2), .out(adder_1_out));  // open: cin, cout
  Register #(.width(32)) register_21 (.D(in_10), .en(L5), .Q(out5), .clk(in_6), .clr(in_4));
  Register #(.width(32)) register_22 (.D(in_10), .en(L13), .Q(out13), .clk(in_6), .clr(in_4));
  Register #(.width(32)) register_23 (.D(in_10), .en(L21), .Q(out21), .clk(in_6), .clr(in_4));
  Register #(.width(32)) register_24 (.D(in_10), .en(L29), .Q(out29), .clk(in_6), .clr(in_4));
  Multiplexer #(.width(32), .enable("false")) multiplexer_1 (
    .in0(subtractor_1_out), .in1(adder_1_out), .out(SP), .sel(in_9));
  Register #(.width(32)) register_25 (.D(in_10), .en(L6), .Q(out6), .clk(in_6), .clr(in_4));
  Register #(.width(32)) register_26 (.D(in_10), .en(L14), .Q(out14), .clk(in_6), .clr(in_4));
  Register #(.width(32)) register_27 (.D(in_10), .en(L22), .Q(out22), .clk(in_6), .clr(in_4));
  Register #(.width(32)) register_28 (.D(in_10), .en(L30), .Q(out30), .clk(in_6), .clr(in_4));
  Register #(.width(32)) register_29 (.D(in_10), .en(L7), .Q(out7), .clk(in_6), .clr(in_4));
  Register #(.width(32)) register_30 (.D(in_10), .en(L15), .Q(out15), .clk(in_6), .clr(in_4));
  Register #(.width(32)) register_31 (.D(in_10), .en(L23), .Q(out23), .clk(in_6), .clr(in_4));
  Multiplexer #(.width(32), .enable("false")) multiplexer_2 (
    .in0(SP), .in1(in_10), .out(multiplexer_2_out), .sel(input31));
  or or_2 (or_2_out, L31, input31);
  Register #(.width(32)) register_32 (.D(multiplexer_2_out), .en(or_2_out), .Q(Output_2), .clk(in_6), .clr(in_4));
  Multiplexer #(.select(5), .width(32), .enable("false")) multiplexer_3 (
    .in0(out0), .in1(out1), .in2(out2), .in3(out3), .in4(out4), .in5(out5), .in6(out6), .in7(out7),
    .in8(out8), .in9(out9), .in10(out10), .in11(out11), .in12(out12), .in13(out13), .in14(out14),
    .in15(out15), .in16(out16), .in17(out17), .in18(out18), .in19(out19), .in20(out20), .in21(out21),
    .in22(out22), .in23(out23), .in24(out24), .in25(out25), .in26(out26), .in27(out27), .in28(out28),
    .in29(out29), .in30(out30), .in31(Output_2), .out(Output), .sel(in_1));
  Multiplexer #(.select(5), .width(32), .enable("false")) multiplexer_4 (
    .in0(out0), .in1(out1), .in2(out2), .in3(out3), .in4(out4), .in5(out5), .in6(out6), .in7(out7),
    .in8(out8), .in9(out9), .in10(out10), .in11(out11), .in12(out12), .in13(out13), .in14(out14),
    .in15(out15), .in16(out16), .in17(out17), .in18(out18), .in19(out19), .in20(out20), .in21(out21),
    .in22(out22), .in23(out23), .in24(out24), .in25(out25), .in26(out26), .in27(out27), .in28(out28),
    .in29(out29), .in30(out30), .in31(Output_2), .out(Output_3), .sel(in_2));
  // Probe on in_1

  // Other names for the same wires on the sheet: clock = in_6; input[31:0] = in_10; memR_W = in_7;
  //   out31[31:0] = Output_2; outA[4:0] = in_1; outB[4:0] = in_2; pop = in_9; push = in_8; reset = in_4;
  //   select[4:0] = in_3; write = in_5

  // Notes on the sheet:
  //   Register File
endmodule

module RF_Input (
  input  [31:0] in_1,
  input  [31:0] in_2,
  input  [31:0] in_3,
  input  [31:0] in_4,
  input  [31:0] in_5,
  input  in_6,
  input  in_7,
  input  in_8,
  input  in_9,
  input  in_10,
  input  in_11,
  input  [6:0] in_12,
  output [31:0] Output
);

  wire [2:0] selector;
  wire [31:0] KBD;

  assign KBD = {{25{1'b0}}, in_12};  // Bit_Extender bit_extender_1
  or or_1 (selector[0], in_6, in_8, in_9, in_11);
  or or_2 (selector[1], in_7, in_9);
  or or_3 (selector[2], in_10, in_11);
  Multiplexer #(.select(3), .width(32), .enable("false")) multiplexer_1 (
    .in0(in_1), .in1(in_5), .in2(in_3), .in3(in_4), .in4(in_2), .in5(KBD), .out(Output), .sel(selector));  // open: in6, in7

  // Other names for the same wires on the sheet: ALU[31:0] = in_1; HI[31:0] = in_3; is_kbd = in_11; is_rnd = in_10;
  //   LO[31:0] = in_4; lw = in_6; memoryA[31:0] = in_5; mfhi = in_7; mflo = in_9; pop = in_8; RND[31:0] = in_2

  // Notes on the sheet:
  //   RF Input
endmodule

module Instruction_Decoder (
  input  clock,
  input  reset,
  input  enable,
  input  [31:0] in_4,
  output [4:0] Output,
  output [25:0] Output_2,
  output [4:0] Output_3,
  output [15:0] Output_4,
  output [4:0] Output_5,
  output Output_6,
  output Output_7,
  output Output_8,
  output Output_9,
  output Output_10,
  output Output_11,
  output Output_12,
  output Output_13,
  output Output_14,
  output Output_15,
  output Output_16,
  output Output_17,
  output Output_18,
  output Output_19,
  output Output_20,
  output Output_21,
  output Output_22,
  output Output_23,
  output Output_24,
  output Output_25,
  output Output_26,
  output Output_27,
  output Output_28,
  output Output_29,
  output Output_30,
  output Output_31,
  output Output_32,
  output Output_33,
  output Output_34,
  output Output_35,
  output Output_36,
  output Output_37,
  output Output_38,
  output Output_39,
  output Output_40,
  output Output_41,
  output [3:0] selector,
  output I,
  output sign
);

  wire _000000, _111111, AND, comparator_16_eq, comparator_17_eq, comparator_18_eq, comparator_19_eq,
       comparator_20_eq, comparator_21_eq, comparator_22_eq, comparator_23_eq, comparator_24_eq,
       comparator_25_eq, comparator_26_eq, comparator_27_eq, comparator_28_eq, comparator_29_eq,
       comparator_30_eq, comparator_31_eq, comparator_32_eq, comparator_33_eq, comparator_34_eq,
       comparator_35_eq, comparator_36_eq, comparator_37_eq, comparator_38_eq, comparator_39_eq, DIV, MUL,
       OR, or_12_out, SLT, SLTI;
  wire [5:0] OP;

  Comparator #(.width(6)) comparator_1 (.a(OP), .b(6'b001000), .eq(Output_8));  // open: gt, lt
  Comparator #(.width(6)) comparator_2 (.a(OP), .b(6'b001010), .eq(Output_12));  // open: gt, lt
  Comparator #(.width(6)) comparator_3 (.a(OP), .b(6'b001011), .eq(Output_16));  // open: gt, lt
  Comparator #(.width(6)) comparator_4 (.a(OP), .b(6'b001100), .eq(Output_20));  // open: gt, lt
  Comparator #(.width(6)) comparator_5 (.a(OP), .b(6'b001101), .eq(Output_24));  // open: gt, lt
  Comparator #(.width(6)) comparator_6 (.a(OP), .b(6'b001110), .eq(Output_28));  // open: gt, lt
  Comparator #(.width(6)) comparator_7 (.a(OP), .b({6{1'b1}}), .eq(_111111));  // open: gt, lt
  Comparator #(.width(6)) comparator_8 (.a(OP), .b({6{1'b0}}), .eq(_000000));  // open: gt, lt
  or or_1 (MUL, Output_18, Output_22);
  or or_2 (DIV, Output_26, Output_30);
  or or_3 (SLT, Output_7, Output_11);
  or or_4 (SLTI, Output_12, Output_16);
  Comparator #(.width(6)) comparator_9 (.a(OP), .b(6'b100011), .eq(Output_31));  // open: gt, lt
  Comparator #(.width(6)) comparator_10 (.a(OP), .b(6'b101011), .eq(Output_9));  // open: gt, lt
  Comparator #(.width(6)) comparator_11 (.a(OP), .b(6'b000100), .eq(Output_13));  // open: gt, lt
  Comparator #(.width(6)) comparator_12 (.a(OP), .b(6'b000101), .eq(Output_17));  // open: gt, lt
  Comparator #(.width(6)) comparator_13 (.a(OP), .b(6'b000110), .eq(Output_21));  // open: gt, lt
  Comparator #(.width(6)) comparator_14 (.a(OP), .b(6'b000111), .eq(Output_25));  // open: gt, lt
  Comparator #(.width(6)) comparator_15 (.a(OP), .b(6'b000001), .eq(Output_29));  // open: gt, lt
  // Probe on {Output_2[7:0], Output_2[15:8], Output[2:0], Output_2[20:16], OP, Output[4:3]}
  Register #(.width(32)) register_1 (
    .D(in_4), .en(enable),
    .Q({Output_2[7:0], Output_2[15:8], Output[2:0], Output_2[20:16], OP, Output[4:3]}), .clk(clock),
    .clr(reset));
  or or_5 (AND, Output_15, Output_20);
  or or_6 (OR, Output_19, Output_24);
  or or_7 (selector[3], Output_27, Output_28);
  Comparator #(.width(6)) comparator_16 (.a(Output_2[5:0]), .b({6{1'b0}}), .eq(comparator_16_eq));  // open: gt, lt
  Comparator #(.width(6)) comparator_17 (.a(Output_2[5:0]), .b(6'b100000), .eq(comparator_17_eq));  // open: gt, lt
  Comparator #(.width(6)) comparator_18 (.a(Output_2[5:0]), .b(6'b100010), .eq(comparator_18_eq));  // open: gt, lt
  Comparator #(.width(6)) comparator_19 (.a(Output_2[5:0]), .b(6'b011000), .eq(comparator_19_eq));  // open: gt, lt
  Comparator #(.width(6)) comparator_20 (.a(Output_2[5:0]), .b(6'b011001), .eq(comparator_20_eq));  // open: gt, lt
  Comparator #(.width(6)) comparator_21 (.a(Output_2[5:0]), .b(6'b011010), .eq(comparator_21_eq));  // open: gt, lt
  Comparator #(.width(6)) comparator_22 (.a(Output_2[5:0]), .b(6'b011011), .eq(comparator_22_eq));  // open: gt, lt
  Comparator #(.width(6)) comparator_23 (.a(Output_2[5:0]), .b(6'b101010), .eq(comparator_23_eq));  // open: gt, lt
  Comparator #(.width(6)) comparator_24 (.a(OP), .b(6'b111000), .eq(comparator_24_eq));  // open: gt, lt
  Comparator #(.width(6)) comparator_25 (.a(Output_2[5:0]), .b({6{1'b0}}), .eq(comparator_25_eq));  // open: gt, lt
  Comparator #(.width(6)) comparator_26 (.a(OP), .b(6'b111000), .eq(comparator_26_eq));  // open: gt, lt
  Comparator #(.width(6)) comparator_27 (.a(Output_2[5:0]), .b(6'b000001), .eq(comparator_27_eq));  // open: gt, lt
  // Probe on OP
  and and_1 (Output_6, _000000, comparator_16_eq);
  and and_2 (Output_10, _000000, comparator_17_eq);
  and and_3 (Output_14, _000000, comparator_18_eq);
  and and_4 (Output_18, _000000, comparator_19_eq);
  and and_5 (Output_22, _000000, comparator_20_eq);
  and and_6 (Output_26, _000000, comparator_21_eq);
  and and_7 (Output_30, _000000, comparator_22_eq);
  and and_8 (Output_7, _000000, comparator_23_eq);
  and and_9 (Output_32, comparator_24_eq, comparator_25_eq);
  and and_10 (Output_34, comparator_26_eq, comparator_27_eq);
  or or_8 (selector[0], Output_14, DIV, AND, Output_23);
  // Probe on Output
  Comparator #(.width(6)) comparator_28 (.a(Output_2[5:0]), .b(6'b101011), .eq(comparator_28_eq));  // open: gt, lt
  Comparator #(.width(6)) comparator_29 (.a(Output_2[5:0]), .b(6'b100100), .eq(comparator_29_eq));  // open: gt, lt
  Comparator #(.width(6)) comparator_30 (.a(Output_2[5:0]), .b(6'b100101), .eq(comparator_30_eq));  // open: gt, lt
  Comparator #(.width(6)) comparator_31 (.a(Output_2[5:0]), .b(6'b100111), .eq(comparator_31_eq));  // open: gt, lt
  Comparator #(.width(6)) comparator_32 (.a(Output_2[5:0]), .b(6'b101000), .eq(comparator_32_eq));  // open: gt, lt
  Comparator #(.width(6)) comparator_33 (.a(Output_2[5:0]), .b(6'b001000), .eq(comparator_33_eq));  // open: gt, lt
  Comparator #(.width(6)) comparator_34 (.a(Output_2[5:0]), .b(6'b010000), .eq(comparator_34_eq));  // open: gt, lt
  Comparator #(.width(6)) comparator_35 (.a(Output_2[5:0]), .b(6'b010010), .eq(comparator_35_eq));  // open: gt, lt
  Comparator #(.width(6)) comparator_36 (.a(Output_2[5:0]), .b({6{1'b1}}), .eq(comparator_36_eq));  // open: gt, lt
  Comparator #(.width(6)) comparator_37 (.a(Output_2[5:0]), .b(6'b000001), .eq(comparator_37_eq));  // open: gt, lt
  Comparator #(.width(6)) comparator_38 (.a(Output_2[5:0]), .b(6'b000010), .eq(comparator_38_eq));  // open: gt, lt
  Comparator #(.width(6)) comparator_39 (.a(Output_2[5:0]), .b(6'b000100), .eq(comparator_39_eq));  // open: gt, lt
  and and_11 (Output_11, _000000, comparator_28_eq);
  and and_12 (Output_15, _000000, comparator_29_eq);
  and and_13 (Output_19, _000000, comparator_30_eq);
  and and_14 (Output_23, _000000, comparator_31_eq);
  and and_15 (Output_27, _000000, comparator_32_eq);
  and and_16 (Output_36, _000000, comparator_33_eq);
  and and_17 (Output_39, _000000, comparator_34_eq);
  and and_18 (Output_41, _000000, comparator_35_eq);
  and and_19 (Output_33, _111111, comparator_36_eq);
  and and_20 (Output_35, _111111, comparator_37_eq);
  and and_21 (Output_37, _111111, comparator_38_eq);
  and and_22 (Output_40, _111111, comparator_39_eq);
  or or_9 (selector[2], SLT, SLTI, OR, AND, Output_23);
  or or_10 (selector[1], MUL, DIV, OR, Output_23);
  or or_11 (sign, Output_18, Output_26, Output_7, Output_12);
  Comparator #(.width(6)) comparator_40 (.a(OP), .b(6'b000010), .eq(Output_38));  // open: gt, lt
  or or_12 (or_12_out, Output_9, Output_8, Output_31);
  or or_13 (I, or_12_out, SLTI, Output_20, Output_24, Output_28);

  assign Output_2[25:21] = Output;
  assign Output_3 = Output_2[20:16];
  assign Output_4 = Output_2[15:0];
  assign Output_5 = Output_2[15:11];

  // Other names for the same wires on the sheet: constant[15:0] = Output_2[15:0];
  //   dest[25:0] = {Output, Output_2[20:0]}; FC[5:0] = Output_2[5:0]; RD[4:0] = Output_2[15:11];
  //   RT[4:0] = Output_2[20:16]; RS[4:0] = Output; add = Output_10; addi = Output_8; and_t = Output_15;
  //   andi = Output_20; beq = Output_13; bgtz = Output_25; blez = Output_21; bltz = Output_29; bne = Output_17;
  //   div_t = Output_26; divu = Output_30; halt = Output_33; j = Output_38; jr = Output_36; kbd = Output_40;
  //   lw = Output_31; mfhi = Output_39; mflo = Output_41; mult = Output_18; mulu = Output_22; nop = Output_6;
  //   nor = Output_23; or_t = Output_19; ori = Output_24; pop = Output_32; push = Output_34; rnd = Output_37;
  //   _0 = selector[0]; _1 = selector[1]; _2 = selector[2]; _3 = selector[3]; XOR = selector[3]; slt_t = Output_7;
  //   slti_t = Output_12; sltiu = Output_16; sltu = Output_11; sub = Output_14; sw = Output_9; tty = Output_35;
  //   xor_t = Output_27; xori = Output_28

  // Notes on the sheet:
  //   Instruction Decoder
  //   Instrucciones Tipo R
  //   Instrucciones Tipo I
  //   Instrucciones Tipo J
endmodule

module Data_Path (
  input  [31:0] in_1,
  input  [6:0] in_2,
  input  in_3,
  input  in_4,
  input  in_5,
  input  in_6,
  input  in_7,
  input  in_8,
  input  in_9,
  output Output,
  output Output_2,
  output Output_3,
  output Output_4,
  output Output_5,
  output Output_6,
  output Output_7,
  output Output_8,
  output [6:0] Output_9,
  output [31:0] Output_10,
  output [31:0] R_out
);

  wire ADD, add_t, addi, AND, and_1_out, and_t, andi, beq, bgtz, blez, bltz, bne, DIV, div_t, divu, I, j, jr,
       kbd, lw, mfhi, mflo, MUL, mult, mulu, nop, \nor , OR, or_t, ori, pop, push, rnd, sign, SLT, slt_t,
       SLTI, slti_t, sltiu, sltu, sub, sw, XOR, xor_t, xori;
  wire [3:0] ALU_selector;
  wire [4:0] multiplexer_1_out, RD, RS, RT;
  wire [15:0] bit_extender_1_out, \const ;
  wire [25:0] dest;
  wire [31:0] ALUout, HI, LO, multiplexer_2_out, PCout, random_1_out, rf_input_1_output, RT_t, SP;
  wire [31:7] RS_t;

  // Probe on RS
  // Probe on RT
  or or_1 (Output_6, beq, bltz, bne, bgtz, blez, j, jr, nop);
  or or_2 (Output_5, rnd, mflo, kbd, mfhi, Output_3);
  // Probe on RD
  Random #(.width(32)) random_1 (.clk(in_3), .next(rnd), .out(random_1_out));  // open: clr
  Instruction_Decoder instruction_decoder_1 (
    .Output(RS), .Output_2(dest), .in_4(in_1), .Output_3(RT), .Output_4(\const ), .Output_5(RD),
    .Output_8(addi), .Output_6(nop), .Output_7(slt_t), .Output_12(slti_t), .Output_13(beq),
    .Output_10(add_t), .Output_11(sltu), .Output_16(sltiu), .Output_17(bne), .Output_14(sub),
    .Output_15(and_t), .Output_20(andi), .Output_21(blez), .Output_18(mult), .Output_19(or_t),
    .Output_24(ori), .Output_25(bgtz), .Output_22(mulu), .Output_23(\nor ), .Output_28(xori),
    .Output_29(bltz), .Output_26(div_t), .Output_27(xor_t), .Output_31(lw), .Output_30(divu),
    .Output_32(pop), .Output_33(Output), .Output_34(push), .Output_35(Output_3), .Output_36(jr),
    .Output_37(rnd), .Output_39(mfhi), .Output_40(kbd), .Output_38(j), .Output_41(mflo), .Output_9(sw),
    .reset(in_5), .enable(in_7), .clock(in_3), .sign(sign), .I(I), .selector(ALU_selector));
  Program_Counter program_counter_1 (
    .in_1(dest), .in_2({RS_t, Output_9}), .in_3(RT_t), .in_4(\const ), .in_5(beq), .in_6(bne), .in_7(blez),
    .in_9(bgtz), .in_10(bltz), .in_11(jr), .in_8(j), .Output(PCout), .enable(in_8), .clock(in_3), .reset(in_5));
  or or_3 (Output_4, sw, lw);
  or or_4 (Output_7, pop, push);
  or or_5 (Output_8, sw, push);
  RF_Input rf_input_1 (
    .in_12(in_2), .in_1(ALUout), .in_6(lw), .in_2(random_1_out), .in_8(pop), .in_7(mfhi), .in_5(in_1),
    .in_9(mflo), .in_10(rnd), .in_11(kbd), .in_3(HI), .in_4(LO), .Output(rf_input_1_output));
  Multiplexer #(.width(5), .enable("false")) multiplexer_1 (.in0(RD), .in1(RT), .out(multiplexer_1_out), .sel(I));
  Memory_Address memory_address_1 (
    .in_1(PCout), .in_4(ALUout), .in_7(SP), .in_2(lw), .in_5(pop), .in_8(in_9), .in_3(sw), .in_6(push),
    .Output(Output_10), .in_10(in_7), .in_9(in_3));
  and and_1 (and_1_out, \const [15], ~ori, ~andi, ~xori);  // AND_Gate
  or or_6 (MUL, mult, mulu);
  or or_7 (DIV, div_t, divu);
  or or_8 (SLT, slt_t, sltu);
  or or_9 (SLTI, slti_t, sltiu);
  Register_File register_file_1 (
    .in_4(in_5), .in_5(in_4), .in_8(push), .in_10(rf_input_1_output), .in_6(in_3), .in_7(in_8), .in_9(pop),
    .in_3(multiplexer_1_out), .in_1(RS), .in_2(RT), .Output({RS_t, Output_9}), .Output_3(RT_t), .Output_2(SP));
  assign bit_extender_1_out = {{15{and_1_out}}, and_1_out};  // Bit_Extender bit_extender_1
  Multiplexer #(.width(32), .enable("false")) multiplexer_2 (
    .in0(RT_t), .in1({bit_extender_1_out, \const }), .out(multiplexer_2_out), .sel(I));
  or or_10 (AND, and_t, andi);
  or or_11 (OR, or_t, ori);
  or or_12 (XOR, xor_t, xori);
  or or_13 (ADD, add_t, addi);
  // Probe on ALUout
  ALU alu_1 (
    .in_2(sign), .Input({RS_t, Output_9}), .Input_2(multiplexer_2_out), .in_5(ALU_selector), .Output(ALUout),
    .Output_2(LO), .Output_3(HI), .in_1(in_3));
  or or_14 (Output_2, MUL, DIV, SLT, SLTI, AND, OR, XOR, ADD, \nor , sub);
  Multiplexer #(.width(32), .enable("false")) multiplexer_3 (.in0({RS_t, Output_9}), .in1(RT_t), .out(R_out), .sel(sw));

  // Other names for the same wires on the sheet: address[31:0] = Output_10; ALU_inst = Output_2; clock = in_3;
  //   enGI = in_7; enPC = in_8; enRF = in_4; halt = Output; instruction[31:0] = in_1; jmp_inst = Output_6;
  //   KBDava = in_6; KBDdata[6:0] = in_2; mem_inst = Output_4; nexti = in_9; R_inst = Output_5; reset = in_5;
  //   RS_t[6:0] = Output_9; tty_data[6:0] = Output_9; stack_inst = Output_7; tty = Output_3; write_inst = Output_8

  // Notes on the sheet:
  //   DATA PATH
endmodule

module Memory_Address (
  input  [31:0] in_1,
  input  in_2,
  input  in_3,
  input  [31:0] in_4,
  input  in_5,
  input  in_6,
  input  [31:0] in_7,
  input  in_8,
  input  in_9,
  input  in_10,
  output [31:0] Output
);

  wire d_ff_1_q, d_ff_2_q, t_ff_1_q;
  wire [1:0] or_2_out;
  wire [31:0] multiplexer_1_out, multiplexer_2_out, subtractor_1_out;

  Subtractor #(.width(32)) subtractor_1 (.a(in_7), .b(32'h4), .out(subtractor_1_out));  // open: bin, bout
  Multiplexer #(.width(32), .enable("false")) multiplexer_1 (
    .in0(in_7), .in1(subtractor_1_out), .out(multiplexer_1_out), .sel(in_6));
  or or_1 (or_2_out[1], in_5, in_6);
  Multiplexer #(.select(2), .width(32), .enable("false")) multiplexer_2 (
    .in0(in_1), .in1(in_4), .in2(multiplexer_1_out), .out(multiplexer_2_out), .sel(or_2_out));  // open: in3
  or or_2 (or_2_out[0], in_2, in_3);
  D_Flip_Flop #(.trigger("falling")) d_ff_1 (
    .clk(in_9), .D(in_10), .Q(d_ff_1_q), .reset(d_ff_2_q));  // open: Qn, preset, en
  Multiplexer #(.width(32), .enable("false")) multiplexer_3 (
    .in0(multiplexer_2_out), .in1(in_1), .out(Output), .sel(t_ff_1_q));
  T_Flip_Flop t_ff_1 (.Q(t_ff_1_q), .preset(in_8), .reset(d_ff_1_q));  // open: clk, T, Qn, en
  D_Flip_Flop #(.trigger("falling")) d_ff_2 (.clk(in_9), .D(d_ff_1_q), .Q(d_ff_2_q));  // open: Qn, preset, en, reset

  // Other names for the same wires on the sheet: ALU[31:0] = in_4; CLK = in_9; getInst = in_8; lw = in_2;
  //   PC[31:0] = in_1; pop = in_5; push = in_6; readyInst = in_10; SP[31:0] = in_7; sw = in_3

  // Notes on the sheet:
  //   MEMORY ADDRESS
endmodule

module Program_Counter (
  input  [25:0] in_1,
  input  [31:0] in_2,
  input  [31:0] in_3,
  input  [15:0] in_4,
  input  in_5,
  input  in_6,
  input  in_7,
  input  in_8,
  input  in_9,
  input  in_10,
  input  in_11,
  input  enable,
  input  clock,
  input  reset,
  output [31:0] Output
);

  wire and_1_out, and_2_out, and_3_out, and_4_out, and_5_out, comparator_1_eq, or_1_out, RS_0, RS__0, RS__RT;
  wire [1:0] or_3_out;
  wire [13:0] bit_extender_1_out;
  wire [31:0] multiplexer_1_out, PC_4, PC_4_const;

  and and_1 (and_1_out, in_5, RS__RT);
  and and_2 (and_2_out, ~RS__RT, in_6);  // AND_Gate
  and and_3 (and_3_out, in_7, RS__0);
  and and_4 (and_4_out, ~RS__0, in_9);  // AND_Gate
  and and_5 (and_5_out, RS_0, in_10);
  Comparator #(.width(32)) comparator_1 (.a(in_2), .b({32{1'b0}}), .eq(comparator_1_eq), .lt(RS_0));  // open: gt
  Comparator #(.width(32)) comparator_2 (.a(in_2), .b(in_3), .eq(RS__RT));  // open: gt, lt
  Adder #(.width(32)) adder_1 (.a(Output), .b(32'h4), .out(PC_4));  // open: cin, cout
  assign bit_extender_1_out = {{13{in_4[15]}}, in_4[15]};  // Bit_Extender bit_extender_1
  or or_1 (or_1_out, and_1_out, and_2_out, and_3_out, and_4_out, and_5_out);
  or or_2 (RS__0, comparator_1_eq, RS_0);
  Adder #(.width(32)) adder_2 (.a(PC_4), .b({bit_extender_1_out, in_4, 2'b00}), .out(PC_4_const));  // open: cin, cout
  or or_3 (or_3_out[0], or_1_out, in_11);
  or or_4 (or_3_out[1], in_11, in_8);
  Multiplexer #(.select(2), .width(32), .enable("false")) multiplexer_1 (
    .in0(PC_4), .in1(PC_4_const), .in2({Output[31:28], in_1, 2'b00}), .in3(in_2), .out(multiplexer_1_out),
    .sel(or_3_out));
  Register #(.width(32)) Program_Counter (.D(multiplexer_1_out), .en(enable), .Q(Output), .clk(clock), .clr(reset));

  // Other names for the same wires on the sheet: const[15:0] = in_4; beq = in_5; bgtz = in_9; blez = in_7;
  //   bltz = in_10; bne = in_6; enPC = enable; j = in_8; dest[25:0] = in_1; jmp[31:2] = {Output[31:28], in_1};
  //   PC[31:0] = Output; jr = in_11; RS[31:0] = in_2; RT[31:0] = in_3

  // Notes on the sheet:
  //   PROGRAM COUNTER
endmodule

module Control_Unit (
  input  in_1,
  input  in_2,
  input  in_3,
  input  in_4,
  input  in_5,
  input  in_6,
  input  in_7,
  input  in_8,
  input  in_9,
  input  in_10,
  input  in_11,
  input  in_12,
  output Output,
  output Output_2,
  output Output_3,
  output Output_4,
  output Output_5,
  output Output_6,
  output Output_7,
  output Output_8
);

  wire branch, d_ff_1_q, d_ff_3_q, d_ff_4_q, d_ff_6_q, demultiplexer_1_out0, demultiplexer_1_out1, or_3_out,
       RF;
  wire [2:0] or_4_out;

  or or_1 (or_4_out[2], in_8, in_11);
  D_Flip_Flop #(.trigger("falling")) d_ff_1 (.clk(in_1), .D(in_5), .Q(d_ff_1_q));  // open: Qn, preset, en, reset
  and and_1 (Output_6, Output_7, in_3);
  Demultiplexer #(.select(3), .enable("false")) demultiplexer_1 (
    .out0(demultiplexer_1_out0), .out1(demultiplexer_1_out1), .out2(branch), .out3(RF), .out4(Output_5),
    .out5(Output_8), .in(d_ff_1_q), .sel(or_4_out));  // open: out6, out7
  or or_2 (or_4_out[1], in_9, in_7);
  or or_3 (or_3_out, Output_4, demultiplexer_1_out0);
  or or_4 (or_4_out[0], in_9, in_6, in_11);
  D_Flip_Flop #(.trigger("falling")) d_ff_2 (
    .clk(in_1), .D(or_3_out), .Q(Output_4), .reset(in_10));  // open: Qn, preset, en
  D_Flip_Flop #(.trigger("falling")) d_ff_3 (
    .clk(in_1), .D(demultiplexer_1_out1), .Q(d_ff_3_q), .reset(in_10));  // open: Qn, preset, en
  D_Flip_Flop #(.trigger("falling")) d_ff_4 (
    .clk(in_1), .D(in_2), .Q(d_ff_4_q), .reset(in_10));  // open: Qn, preset, en
  or or_5 (Output, d_ff_3_q, in_4, RF);
  D_Flip_Flop #(.trigger("falling")) d_ff_5 (.clk(in_1), .D(Output), .Q(Output_7));  // open: Qn, preset, en, reset
  or or_6 (Output_3, d_ff_4_q, d_ff_6_q);
  D_Flip_Flop #(.trigger("falling")) d_ff_6 (
    .clk(in_1), .D(Output_2), .Q(d_ff_6_q), .reset(in_10));  // open: Qn, preset, en
  or or_7 (Output_2, Output_7, in_12, branch);

  // Other names for the same wires on the sheet: ALU_inst = in_6; clock = in_1; cont = Output_2; PC_enable = Output_2;
  //   end = Output_4; get_data = Output_5; get_inst = Output_3; jmp_inst = in_7; mem_inst = in_8; R_inst = in_9;
  //   ready_data = in_4; ready_inst = in_5; ready_w = in_12; reset = in_10; RF_enable = Output; start = in_2;
  //   kbd_enable = Output_7; tty = Output_7; tty_enable = Output_6; tty_inst = in_3; write = Output_8;
  //   write_inst = in_11

  // Notes on the sheet:
  //   CONTROL UNIT
endmodule

module \Caché_INTERACTION  (
  input  [31:0] bank0,
  input  [31:0] bank1,
  input  [31:0] bank2,
  input  [31:0] bank3,
  input  [31:0] dp_address,
  input  [31:0] in_6,
  input  [3:0] read_time,
  input  [3:0] write_time,
  input  get_data,
  input  write,
  input  get_inst,
  input  clock,
  input  reset,
  output [31:0] Instruction,
  output [15:0] address,
  output [3:0] mask,
  output cs,
  output rw,
  output ready_inst,
  output ready_data,
  output ready_write
);

  wire and_1_out, d_ff_3_q, d_ff_4_q, enable_data, enable_Inst, isIn0, isIn1, isIn2, isIn3, isIn4, isIn5,
       isIn6, isIn7, isIn8, isIn9, isIn10, isIn11, isIn12, isIn13, isIn14, isIn15, isIn16, isIn17, isIn18,
       isIn19, isIn20, isIn21, isIn22, isIn23, isIn24, isIn25, isIn26, isIn27, isIn28, isIn29, isIn30,
       isIn31, isInMemory, L0, L0w, L1, L1w, L2, L2w, L3, L3w, L4, L4w, L5, L5w, L6, L6w, L7, L7w, L8, L8w,
       L9, L9w, L10, L10w, L11, L11w, L12, L12w, L13, L13w, L14, L14w, L15, L15w, L16, L16w, L17, L17w, L18,
       L18w, L19, L19w, L20, L20w, L21, L21w, L22, L22w, L23, L23w, L24, L24w, L25, L25w, L26, L26w, L27,
       L27w, L28, L28w, L29, L29w, L30, L30w, L31, L31w, or_1_out, or_2_out, or_3_out, or_4_out, or_5_out,
       or_6_out, or_7_out, or_8_out, or_9_out, or_10_out, or_11_out, or_12_out, or_13_out, or_14_out,
       or_15_out, or_16_out, or_17_out, or_18_out, or_19_out, or_20_out, or_21_out, or_22_out, or_23_out,
       or_24_out, or_25_out, or_26_out, or_27_out, or_28_out, or_29_out, or_30_out, or_31_out, or_32_out,
       or_33_out, or_34_out, or_35_out, or_36_out, or_37_out, or_38_out, or_39_out, or_40_out, or_41_out,
       or_42_out, or_43_out, ready_ram_data, ready_ram_inst;
  wire [31:0] bank0_t, bank1_t, bank2_t, bank3_t, input0, input1, input2, input3, input4, input5, input6,
       input7, input8, input9, input10, input11, input12, input13, input14, input15, input16, input17,
       input18, input19, input20, input21, input22, input23, input24, input25, input26, input27, input28,
       input29, input30, input31, out0, out1, out2, out3, out4, out5, out6, out7, out8, out9, out10, out11,
       out12, out13, out14, out15, out16, out17, out18, out19, out20, out21, out22, out23, out24, out25,
       out26, out27, out28, out29, out30, out31, out_bank0, out_bank1, out_bank2, out_bank3;

  Multiplexer #(.width(32), .enable("false")) multiplexer_1 (.in0(bank0), .in1(in_6), .out(bank0_t), .sel(write));
  Multiplexer #(.width(32), .enable("false")) multiplexer_2 (.in0(bank2), .in1(in_6), .out(bank2_t), .sel(write));
  Multiplexer #(.select(5)) multiplexer_3 (
    .in0(isIn0), .in1(isIn1), .in2(isIn2), .in3(isIn3), .in4(isIn4), .in5(isIn5), .in6(isIn6), .in7(isIn7),
    .in8(isIn8), .in9(isIn9), .in10(isIn10), .in11(isIn11), .in12(isIn12), .in13(isIn13), .in14(isIn14),
    .in15(isIn15), .in16(isIn16), .in17(isIn17), .in18(isIn18), .in19(isIn19), .in20(isIn20), .in21(isIn21),
    .in22(isIn22), .in23(isIn23), .in24(isIn24), .in25(isIn25), .in26(isIn26), .in27(isIn27), .in28(isIn28),
    .in29(isIn29), .in30(isIn30), .in31(isIn31), .out(isInMemory), .sel(dp_address[6:2]), .en(or_1_out));
  // Probe on dp_address[6:2]
  or or_1 (or_1_out, get_inst, get_data);
  Demultiplexer #(.select(5), .enable("false")) demultiplexer_1 (
    .out0(L0w), .out1(L1w), .out2(L2w), .out3(L3w), .out4(L4w), .out5(L5w), .out6(L6w), .out7(L7w),
    .out8(L8w), .out9(L9w), .out10(L10w), .out11(L11w), .out12(L12w), .out13(L13w), .out14(L14w),
    .out15(L15w), .out16(L16w), .out17(L17w), .out18(L18w), .out19(L19w), .out20(L20w), .out21(L21w),
    .out22(L22w), .out23(L23w), .out24(L24w), .out25(L25w), .out26(L26w), .out27(L27w), .out28(L28w),
    .out29(L29w), .out30(L30w), .out31(L31w), .in(write), .sel(dp_address[6:2]));
  Multiplexer #(.width(32), .enable("false")) multiplexer_4 (.in0(bank1), .in1(in_6), .out(bank1_t), .sel(write));
  Multiplexer #(.width(32), .enable("false")) multiplexer_5 (.in0(bank3), .in1(in_6), .out(bank3_t), .sel(write));
  CACHE_REGISTER cache_register_1 (
    .clock(clock), .reset(reset), .\input (input0), .\type (dp_address[22:7]), .write(or_2_out),
    .Output_2(isIn0), .Output(out0));
  or or_2 (or_2_out, L0, L0w);
  CACHE_REGISTER cache_register_2 (
    .clock(clock), .reset(reset), .\input (input8), .\type (dp_address[22:7]), .write(or_3_out),
    .Output_2(isIn8), .Output(out8));
  or or_3 (or_3_out, L8, L8w);
  CACHE_REGISTER cache_register_3 (
    .clock(clock), .reset(reset), .\input (input16), .\type (dp_address[22:7]), .write(or_4_out),
    .Output_2(isIn16), .Output(out16));
  or or_4 (or_4_out, L16, L16w);
  CACHE_REGISTER cache_register_4 (
    .clock(clock), .reset(reset), .\input (input24), .\type (dp_address[22:7]), .write(or_5_out),
    .Output_2(isIn24), .Output(out24));
  or or_5 (or_5_out, L24, L24w);
  // Probe on out24
  or or_6 (or_6_out, L1, L1w);
  or or_7 (or_7_out, L9, L9w);
  or or_8 (or_8_out, L17, L17w);
  or or_9 (or_9_out, L25, L25w);
  Multiplexer #(.select(3), .width(32)) multiplexer_6 (
    .in0(out0), .in1(out4), .in2(out8), .in3(out12), .in4(out16), .in5(out20), .in6(out24), .in7(out28),
    .out(out_bank0), .sel(dp_address[6:4]), .en(isInMemory));
  Multiplexer #(.select(3), .width(32)) multiplexer_7 (
    .in0(out2), .in1(out6), .in2(out10), .in3(out14), .in4(out18), .in5(out22), .in6(out26), .in7(out30),
    .out(out_bank2), .sel(dp_address[6:4]), .en(isInMemory));
  CACHE_REGISTER cache_register_5 (
    .clock(clock), .reset(reset), .\input (input1), .\type (dp_address[22:7]), .write(or_6_out),
    .Output_2(isIn1), .Output(out1));
  CACHE_REGISTER cache_register_6 (
    .clock(clock), .reset(reset), .\input (input9), .\type (dp_address[22:7]), .write(or_7_out),
    .Output_2(isIn9), .Output(out9));
  CACHE_REGISTER cache_register_7 (
    .clock(clock), .reset(reset), .\input (input17), .\type (dp_address[22:7]), .write(or_8_out),
    .Output_2(isIn17), .Output(out17));
  // Probe on out25
  CACHE_REGISTER cache_register_8 (
    .clock(clock), .reset(reset), .\input (input25), .\type (dp_address[22:7]), .write(or_9_out),
    .Output_2(isIn25), .Output(out25));
  or or_10 (or_10_out, L2, L2w);
  or or_11 (or_11_out, L10, L10w);
  or or_12 (or_12_out, L18, L18w);
  or or_13 (or_13_out, L26, L26w);
  CACHE_REGISTER cache_register_9 (
    .clock(clock), .reset(reset), .\input (input2), .\type (dp_address[22:7]), .write(or_10_out),
    .Output_2(isIn2), .Output(out2));
  CACHE_REGISTER cache_register_10 (
    .clock(clock), .reset(reset), .\input (input10), .\type (dp_address[22:7]), .write(or_11_out),
    .Output_2(isIn10), .Output(out10));
  CACHE_REGISTER cache_register_11 (
    .clock(clock), .reset(reset), .\input (input18), .\type (dp_address[22:7]), .write(or_12_out),
    .Output_2(isIn18), .Output(out18));
  // Probe on out26
  CACHE_REGISTER cache_register_12 (
    .clock(clock), .reset(reset), .\input (input26), .\type (dp_address[22:7]), .write(or_13_out),
    .Output_2(isIn26), .Output(out26));
  Demultiplexer #(.select(3), .width(32)) demultiplexer_2 (
    .out0(input0), .out1(input4), .out2(input8), .out3(input12), .out4(input16), .out5(input20),
    .out6(input24), .out7(input28), .in(bank0_t), .sel(dp_address[6:4]), .en(or_19_out));
  Demultiplexer #(.select(3), .width(32)) demultiplexer_3 (
    .out0(input2), .out1(input6), .out2(input10), .out3(input14), .out4(input18), .out5(input22),
    .out6(input26), .out7(input30), .in(bank2_t), .sel(dp_address[6:4]), .en(or_14_out));
  or or_14 (or_14_out, enable_data, write, enable_Inst);
  CACHE_REGISTER cache_register_13 (
    .clock(clock), .reset(reset), .\input (input3), .\type (dp_address[22:7]), .write(or_15_out),
    .Output_2(isIn3), .Output(out3));
  or or_15 (or_15_out, L3, L3w);
  CACHE_REGISTER cache_register_14 (
    .clock(clock), .reset(reset), .\input (input11), .\type (dp_address[22:7]), .write(or_16_out),
    .Output_2(isIn11), .Output(out11));
  or or_16 (or_16_out, L11, L11w);
  CACHE_REGISTER cache_register_15 (
    .clock(clock), .reset(reset), .\input (input19), .\type (dp_address[22:7]), .write(or_17_out),
    .Output_2(isIn19), .Output(out19));
  or or_17 (or_17_out, L19, L19w);
  // Probe on out27
  CACHE_REGISTER cache_register_16 (
    .clock(clock), .reset(reset), .\input (input27), .\type (dp_address[22:7]), .write(or_18_out),
    .Output_2(isIn27), .Output(out27));
  or or_18 (or_18_out, L27, L27w);
  or or_19 (or_19_out, enable_data, write, enable_Inst);
  or or_20 (or_20_out, L4, L4w);
  or or_21 (or_21_out, L12, L12w);
  or or_22 (or_22_out, L20, L20w);
  or or_23 (or_23_out, L28, L28w);
  or or_24 (or_24_out, enable_data, enable_Inst);
  Demultiplexer #(.select(3), .enable("false")) demultiplexer_4 (
    .out0(L0), .out1(L4), .out2(L8), .out3(L12), .out4(L16), .out5(L20), .out6(L24), .out7(L28),
    .in(or_24_out), .sel(dp_address[6:4]));
  Demultiplexer #(.select(3), .enable("false")) demultiplexer_5 (
    .out0(L2), .out1(L6), .out2(L10), .out3(L14), .out4(L18), .out5(L22), .out6(L26), .out7(L30),
    .in(or_25_out), .sel(dp_address[6:4]));
  or or_25 (or_25_out, enable_data, enable_Inst);
  CACHE_REGISTER cache_register_17 (
    .clock(clock), .reset(reset), .\input (input4), .\type (dp_address[22:7]), .write(or_20_out),
    .Output_2(isIn4), .Output(out4));
  // Probe on out12
  CACHE_REGISTER cache_register_18 (
    .clock(clock), .reset(reset), .\input (input12), .\type (dp_address[22:7]), .write(or_21_out),
    .Output_2(isIn12), .Output(out12));
  CACHE_REGISTER cache_register_19 (
    .clock(clock), .reset(reset), .\input (input20), .\type (dp_address[22:7]), .write(or_22_out),
    .Output_2(isIn20), .Output(out20));
  // Probe on out28
  CACHE_REGISTER cache_register_20 (
    .clock(clock), .reset(reset), .\input (input28), .\type (dp_address[22:7]), .write(or_23_out),
    .Output_2(isIn28), .Output(out28));
  CACHE_REGISTER cache_register_21 (
    .clock(clock), .reset(reset), .\input (input5), .\type (dp_address[22:7]), .write(or_26_out),
    .Output_2(isIn5), .Output(out5));
  or or_26 (or_26_out, L5, L5w);
  // Probe on out13
  CACHE_REGISTER cache_register_22 (
    .clock(clock), .reset(reset), .\input (input13), .\type (dp_address[22:7]), .write(or_27_out),
    .Output_2(isIn13), .Output(out13));
  or or_27 (or_27_out, L13, L13w);
  CACHE_REGISTER cache_register_23 (
    .clock(clock), .reset(reset), .\input (input21), .\type (dp_address[22:7]), .write(or_28_out),
    .Output_2(isIn21), .Output(out21));
  or or_28 (or_28_out, L21, L21w);
  // Probe on out29
  CACHE_REGISTER cache_register_24 (
    .clock(clock), .reset(reset), .\input (input29), .\type (dp_address[22:7]), .write(or_29_out),
    .Output_2(isIn29), .Output(out29));
  or or_29 (or_29_out, L29, L29w);
  Multiplexer #(.select(3), .width(32)) multiplexer_8 (
    .in0(out1), .in1(out5), .in2(out9), .in3(out13), .in4(out17), .in5(out21), .in6(out25), .in7(out29),
    .out(out_bank1), .sel(dp_address[6:4]), .en(isInMemory));
  Multiplexer #(.select(3), .width(32)) multiplexer_9 (
    .in0(out3), .in1(out7), .in2(out11), .in3(out15), .in4(out19), .in5(out23), .in6(out27), .in7(out31),
    .out(out_bank3), .sel(dp_address[6:4]), .en(isInMemory));
  CACHE_REGISTER cache_register_25 (
    .clock(clock), .reset(reset), .\input (input6), .\type (dp_address[22:7]), .write(or_30_out),
    .Output_2(isIn6), .Output(out6));
  or or_30 (or_30_out, L6, L6w);
  CACHE_REGISTER cache_register_26 (
    .clock(clock), .reset(reset), .\input (input14), .\type (dp_address[22:7]), .write(or_31_out),
    .Output_2(isIn14), .Output(out14));
  or or_31 (or_31_out, L14, L14w);
  CACHE_REGISTER cache_register_27 (
    .clock(clock), .reset(reset), .\input (input22), .\type (dp_address[22:7]), .write(or_32_out),
    .Output_2(isIn22), .Output(out22));
  or or_32 (or_32_out, L22, L22w);
  CACHE_REGISTER cache_register_28 (
    .clock(clock), .reset(reset), .\input (input30), .\type (dp_address[22:7]), .write(or_33_out),
    .Output_2(isIn30), .Output(out30));
  or or_33 (or_33_out, L30, L30w);
  // Probe on out14
  // Probe on out30
  or or_34 (or_34_out, L7, L7w);
  or or_35 (or_35_out, L15, L15w);
  or or_36 (or_36_out, L23, L23w);
  or or_37 (or_37_out, L31, L31w);
  CACHE_REGISTER cache_register_29 (
    .clock(clock), .reset(reset), .\input (input7), .\type (dp_address[22:7]), .write(or_34_out),
    .Output_2(isIn7), .Output(out7));
  // Probe on out15
  CACHE_REGISTER cache_register_30 (
    .clock(clock), .reset(reset), .\input (input15), .\type (dp_address[22:7]), .write(or_35_out),
    .Output_2(isIn15), .Output(out15));
  CACHE_REGISTER cache_register_31 (
    .clock(clock), .reset(reset), .\input (input23), .\type (dp_address[22:7]), .write(or_36_out),
    .Output_2(isIn23), .Output(out23));
  // Probe on out31
  CACHE_REGISTER cache_register_32 (
    .clock(clock), .reset(reset), .\input (input31), .\type (dp_address[22:7]), .write(or_37_out),
    .Output_2(isIn31), .Output(out31));
  Demultiplexer #(.select(3), .width(32)) demultiplexer_6 (
    .out0(input1), .out1(input5), .out2(input9), .out3(input13), .out4(input17), .out5(input21),
    .out6(input25), .out7(input29), .in(bank1_t), .sel(dp_address[6:4]), .en(or_38_out));
  or or_38 (or_38_out, enable_data, write, enable_Inst);
  Demultiplexer #(.select(3), .width(32)) demultiplexer_7 (
    .out0(input3), .out1(input7), .out2(input11), .out3(input15), .out4(input19), .out5(input23),
    .out6(input27), .out7(input31), .in(bank3_t), .sel(dp_address[6:4]), .en(or_39_out));
  or or_39 (or_39_out, enable_data, write, enable_Inst);
  and and_1 (and_1_out, get_data, isInMemory);
  Demultiplexer #(.select(3), .enable("false")) demultiplexer_8 (
    .out0(L1), .out1(L5), .out2(L9), .out3(L13), .out4(L17), .out5(L21), .out6(L25), .out7(L29),
    .in(or_42_out), .sel(dp_address[6:4]));
  Ask_RAM ask_ram_1 (
    .dp_address(dp_address), .address(address), .mask(mask), .read_time(read_time), .write_time(write_time),
    .cs(cs), .rw(rw), .ready_inst(ready_ram_inst), .get_data(get_data), .write(write), .get_inst(get_inst),
    .ready_data(ready_ram_data), .ready_write(ready_write), .clock(clock), .reset(reset),
    .isInMemory(isInMemory), .Output_2(enable_data), .Output(enable_Inst));
  or or_40 (or_40_out, isInMemory, ready_ram_inst);
  or or_41 (or_41_out, and_1_out, ready_ram_data);
  or or_42 (or_42_out, enable_data, enable_Inst);
  Demultiplexer #(.select(3), .enable("false")) demultiplexer_9 (
    .out0(L3), .out1(L7), .out2(L11), .out3(L15), .out4(L19), .out5(L23), .out6(L27), .out7(L31),
    .in(or_43_out), .sel(dp_address[6:4]));
  or or_43 (or_43_out, enable_data, enable_Inst);
  D_Flip_Flop #(.trigger("falling")) d_ff_1 (
    .clk(clock), .D(or_40_out), .Q(ready_inst), .reset(d_ff_3_q));  // open: Qn, preset, en
  D_Flip_Flop #(.trigger("falling")) d_ff_2 (
    .clk(clock), .D(or_41_out), .Q(ready_data), .reset(d_ff_4_q));  // open: Qn, preset, en
  D_Flip_Flop #(.trigger("falling")) d_ff_3 (.clk(clock), .D(ready_inst), .Q(d_ff_3_q));  // open: Qn, preset, en, reset
  D_Flip_Flop #(.trigger("falling")) d_ff_4 (.clk(clock), .D(ready_data), .Q(d_ff_4_q));  // open: Qn, preset, en, reset
  // Probe on Instruction
  Multiplexer #(.select(2), .width(32), .enable("false")) multiplexer_10 (
    .in0(out_bank0), .in1(out_bank1), .in2(out_bank2), .in3(out_bank3), .out(Instruction),
    .sel(dp_address[3:2]));

  // Other names for the same wires on the sheet: select[4:0] = dp_address[6:2]; C_address[15:0] = dp_address[22:7];
  //   R_out[31:0] = in_6; RAM_OUTPUT_0[31:0] = bank0; RAM_OUTPUT_1[31:0] = bank1; RAM_OUTPUT_2[31:0] = bank2;
  //   RAM_OUTPUT_3[31:0] = bank3

  // Notes on the sheet:
  //   CACHE INTERACTION
  //   Ask Ram
endmodule

module Timer (
  input  in_1,
  input  in_2,
  input  in_3,
  input  [3:0] in_4,
  output Output
);

  wire comparator_1_eq, comparator_1_lt;
  wire [3:0] counter_1_q;

  Counter #(.width(4), .max('hf)) counter_1 (
    .count(in_1), .Q(counter_1_q), .clk(in_3), .clr(in_2));  // open: load, D, carry
  Comparator #(.width(4)) comparator_1 (
    .a(in_4), .b(counter_1_q), .eq(comparator_1_eq), .lt(comparator_1_lt));  // open: gt
  or or_1 (Output, comparator_1_eq, comparator_1_lt);

  // Other names for the same wires on the sheet: clock = in_3; ready = Output; reset = in_2; start = in_1;
  //   wait_time[3:0] = in_4

  // Notes on the sheet:
  //   TIMER
endmodule

module CACHE_REGISTER (
  input  [31:0] \input ,
  input  [15:0] \type ,
  input  write,
  input  clock,
  input  reset,
  output [31:0] Output,
  output Output_2
);

  wire comparator_1_eq, t_ff_1_q;
  wire [15:0] tSave;

  Register #(.width(16)) register_1 (.D(\type ), .en(write), .Q(tSave), .clk(clock), .clr(reset));
  Comparator #(.width(16)) comparator_1 (.a(tSave), .b(\type ), .eq(comparator_1_eq));  // open: gt, lt
  T_Flip_Flop t_ff_1 (.Q(t_ff_1_q), .preset(write));  // open: clk, T, Qn, reset, en
  // Probe on Output
  Register #(.width(32)) register_2 (.D(\input ), .en(write), .Q(Output), .clk(clock), .clr(reset));
  and and_1 (Output_2, comparator_1_eq, t_ff_1_q);

  // Other names for the same wires on the sheet: isIn = Output_2; out0[31:0] = Output

  // Notes on the sheet:
  //   CACHE REGISTER
endmodule

module Ask_RAM (
  input  [31:0] dp_address,
  input  [3:0] read_time,
  input  [3:0] write_time,
  input  get_data,
  input  isInMemory,
  input  write,
  input  get_inst,
  input  clock,
  input  reset,
  output [15:0] address,
  output [3:0] mask,
  output cs,
  output rw,
  output ready_inst,
  output ready_data,
  output ready_write,
  output Output,
  output Output_2
);

  wire a, and_1_out, and_2_out, and_3_out, d_ff_6_q, d_ff_7_q, enable, is_inst, or_2_out, or_3_out, read,
       ready, stop;

  and and_1 (and_1_out, ~isInMemory, get_inst);  // AND_Gate
  and and_2 (and_2_out, ~isInMemory, get_data);  // AND_Gate
  or or_1 (read, and_1_out, and_2_out);
  or or_2 (or_2_out, write, stop);
  D_Flip_Flop #(.trigger("falling")) d_ff_1 (.clk(clock), .D(write), .Q(rw), .en(or_2_out));  // open: Qn, preset, reset
  D_Flip_Flop #(.trigger("falling")) d_ff_2 (.clk(clock), .D(read), .Q(a), .en(or_3_out));  // open: Qn, preset, reset
  or or_3 (or_3_out, read, enable);
  or or_4 (cs, a, enable, rw);
  Timer timer_1 (.in_1(rw), .in_2(ready_write), .in_3(clock), .in_4(write_time), .Output(stop));
  Timer timer_2 (.in_1(a), .in_2(ready), .in_3(clock), .in_4(read_time), .Output(enable));
  D_Flip_Flop d_ff_3 (.clk(clock), .D(enable), .Q(ready));  // open: Qn, preset, en, reset
  D_Flip_Flop #(.trigger("falling")) d_ff_4 (.clk(clock), .D(stop), .Q(ready_write));  // open: Qn, preset, en, reset
  Demultiplexer #(.enable("false")) demultiplexer_1 (.out0(Output_2), .out1(Output), .in(enable), .sel(is_inst));
  // Probe on dp_address[3:2]
  and and_3 (and_3_out, ~isInMemory, get_inst);  // AND_Gate
  Demultiplexer #(.select(2), .enable("false")) demultiplexer_2 (
    .out0(mask[0]), .out1(mask[1]), .out2(mask[2]), .out3(mask[3]), .in(1'b1), .sel(dp_address[3:2]));
  D_Flip_Flop #(.trigger("falling")) d_ff_5 (
    .Q(is_inst), .preset(and_3_out), .reset(d_ff_6_q));  // open: clk, D, Qn, en
  Demultiplexer #(.enable("false")) demultiplexer_3 (.out0(ready_data), .out1(ready_inst), .in(ready), .sel(is_inst));
  D_Flip_Flop #(.trigger("falling")) d_ff_6 (
    .clk(clock), .D(ready), .Q(d_ff_6_q), .reset(d_ff_7_q));  // open: Qn, preset, en
  D_Flip_Flop #(.trigger("falling")) d_ff_7 (.clk(clock), .D(d_ff_6_q), .Q(d_ff_7_q));  // open: Qn, preset, en, reset

  assign address = dp_address[19:4];

  // Other names for the same wires on the sheet: enable_data = Output_2; enable_Inst = Output; stop1 = enable

  // Notes on the sheet:
  //   ASK RAM
endmodule
